# Fritzing sketch diagrama (saved by Fritzing 0.9.0b)
breadboards: 1

parts:
  Arduino = Arduino Micro (Rev3)
  Shift_Register = 74HC595 SMD [package="SO16 [SMD]"]
  Sensor_Temperatura = DS18B20 1-Wire Temperature Sensor [part_number=DS18B20]
  R1 = Resistor [tolerance=±5% resistance=4.7k package=THT]
  CNY70_Cocina = PHOTOTRANSISTOR REFLECTIVE OBJECT SENSOR [package=qrb1114-side]
  R2 = Resistor [tolerance=±10% resistance=22 package=THT]
  R3 = Resistor [tolerance=±5% resistance=47k package=THT]
  CNY70_Cuarto = PHOTOTRANSISTOR REFLECTIVE OBJECT SENSOR [package=qrb1114-side]
  R4 = Resistor [tolerance=±10% resistance=22 package=THT]
  R5 = Resistor [tolerance=±5% resistance=47k package=THT]
  R6 = Resistor [tolerance=±5% resistance=4.7k package=THT]
  LED1_x_6 = LED - 5mm [color="Red (633nm)" package="5 mm [THT]"]

nets:
  GND: Arduino.GND, Shift_Register.GND, Shift_Register.OE, Sensor_Temperatura.GND, R2.Pin_0, R3.Pin_0, R4.Pin_0, R5.Pin_0, LED1_x_6.cathode
  N1: Arduino.D5_PWM, Shift_Register.ST_CP
  N2: Arduino.D6_PWM/A7, Shift_Register.DS
  N3: Arduino.D7, Shift_Register.SH_CP
  N4: Arduino.D11_PWM, Sensor_Temperatura.DQ, R1.Pin_1
  5V: Arduino.VIN, CNY70_Cocina.A, CNY70_Cocina.C, CNY70_Cuarto.A, CNY70_Cuarto.C
  5V_2: Arduino.5V, Shift_Register.MR, Shift_Register.VCC, Sensor_Temperatura.VDD, R1.Pin_0
  N5: Arduino.A1, CNY70_Cocina.K, R2.Pin_1
  N6: Arduino.A0, CNY70_Cuarto.E, R5.Pin_1
  N7: Shift_Register.Q1, R6.Pin_1
  N8: CNY70_Cocina.E, R3.Pin_1
  N9: CNY70_Cuarto.K, R4.Pin_1
  N10: R6.Pin_0, LED1_x_6.anode
